// Logisim project Teste Irrigação.circ as structural Verilog: 1 circuit, main circuit main
module main (
  input  H,
  input  M,
  input  L,
  input  Us,
  input  Ua,
  input  T,
  input  SD
);

  wire and_1_out, and_2_out, and_3_out, and_4_out, and_5_out, and_6_out, and_7_out, and_8_out, and_9_out,
       and_10_out, and_11_out, and_12_out, and_13_out, and_14_out, and_15_out, and_16_out, and_17_out,
       and_18_out, and_19_out, and_20_out, and_21_out, and_22_out, and_23_out, and_24_out, and_25_out,
       nor_1_out, not_1_out, not_2_out, not_3_out, not_4_out, not_5_out, not_6_out, not_7_out, not_8_out,
       not_9_out, not_10_out, not_11_out, not_12_out, not_13_out, not_14_out, not_15_out, not_16_out,
       not_17_out, not_18_out, not_19_out, not_20_out, not_21_out, not_22_out, not_23_out, not_24_out,
       not_25_out, not_26_out, not_27_out, not_28_out, not_29_out, not_30_out, not_31_out, not_32_out,
       not_33_out, not_34_out, not_35_out, not_36_out, not_37_out, not_38_out, not_39_out, not_40_out,
       or_1_out, or_2_out, or_3_out, or_4_out, or_5_out, or_6_out, or_7_out, or_8_out, or_9_out, or_10_out,
       or_11_out, or_12_out, or_13_out, or_14_out, or_15_out, or_16_out;

  not not_1 (not_1_out, H);
  not not_2 (not_2_out, M);
  not not_3 (not_3_out, H);
  not not_4 (not_4_out, H);
  not not_5 (not_5_out, M);
  or or_1 (or_1_out, not_5_out, L);
  not not_6 (not_6_out, M);
  not not_7 (not_7_out, L);
  not not_8 (not_8_out, L);
  and and_1 (and_1_out, not_8_out, M);
  and and_2 (and_2_out, H, not_9_out);
  not not_9 (not_9_out, M);
  not not_10 (not_10_out, M);
  not not_11 (not_11_out, T);
  nor nor_1 (nor_1_out, H, M, L);
  and and_3 (and_3_out, not_1_out, not_2_out, L);
  and and_4 (and_4_out, not_3_out, M, L);
  and and_5 (and_5_out, H, M, L);
  and and_6 (and_6_out, not_4_out, or_1_out);
  or or_2 (or_2_out, not_6_out, not_7_out);
  or or_3 (or_3_out, and_1_out, and_2_out);
  or or_4 (or_4_out, not_10_out, T);
  not not_12 (not_12_out, Ua);
  and and_7 (and_7_out, M, not_11_out);
  and and_8 (and_8_out, Ua, or_4_out);
  not not_13 (not_13_out, or_3_out);
  not not_14 (not_14_out, Us);
  or or_5 (or_5_out, not_12_out, and_7_out);
  LED led_1 (.in(and_6_out));
  LED led_2 (.in(or_2_out));
  and and_9 (and_9_out, not_13_out, not_14_out, L);
  not not_15 (not_15_out, SD);
  and and_10 (and_10_out, not_15_out, nor_1_out);
  not not_16 (not_16_out, SD);
  and and_11 (and_11_out, not_16_out, and_3_out);
  not not_17 (not_17_out, SD);
  and and_12 (and_12_out, not_17_out, and_4_out);
  not not_18 (not_18_out, SD);
  and and_13 (and_13_out, not_18_out, and_5_out);
  and and_14 (and_14_out, and_8_out, and_9_out);
  and and_15 (and_15_out, and_9_out, or_5_out);
  LED led_3 (.in(and_15_out));
  LED led_4 (.in(and_14_out));
  not not_19 (not_19_out, SD);
  and and_16 (and_16_out, or_3_out, not_19_out);
  and and_17 (and_17_out, and_14_out, SD);
  and and_18 (and_18_out, and_15_out, SD);
  LED led_5 (.in(or_6_out));
  or or_6 (or_6_out, or_3_out, and_10_out);
  LED led_6 (.in(or_7_out));
  or or_7 (or_7_out, and_10_out, and_11_out, and_13_out);
  or or_8 (or_8_out, and_11_out, and_12_out);
  LED led_7 (.in(or_8_out));
  or or_9 (or_9_out, and_10_out, and_12_out, and_16_out, and_17_out);
  or or_10 (or_10_out, and_12_out, and_11_out, and_18_out, and_17_out);
  or or_11 (or_11_out, and_16_out, and_18_out, and_13_out, and_17_out);
  not not_20 (not_20_out, or_9_out);
  and and_19 (and_19_out, not_20_out, not_21_out);
  not not_21 (not_21_out, or_11_out);
  or or_12 (or_12_out, or_10_out, not_22_out);
  not not_22 (not_22_out, or_11_out);
  not not_23 (not_23_out, or_9_out);
  not not_24 (not_24_out, or_10_out);
  not not_25 (not_25_out, or_11_out);
  not not_26 (not_26_out, or_10_out);
  not not_27 (not_27_out, or_11_out);
  not not_28 (not_28_out, or_12_out);
  and and_20 (and_20_out, or_10_out, or_11_out, or_9_out);
  and and_21 (and_21_out, or_9_out, or_10_out);
  not not_29 (not_29_out, or_9_out);
  and and_22 (and_22_out, not_29_out, not_30_out);
  not not_30 (not_30_out, or_10_out);
  and and_23 (and_23_out, not_31_out, not_32_out);
  not not_31 (not_31_out, or_9_out);
  not not_32 (not_32_out, or_10_out);
  not not_33 (not_33_out, or_11_out);
  and and_24 (and_24_out, or_10_out, not_33_out);
  not not_34 (not_34_out, and_25_out);
  and and_25 (and_25_out, not_23_out, not_24_out, not_25_out);
  or or_13 (or_13_out, not_26_out, not_27_out);
  not not_35 (not_35_out, or_13_out);
  or or_14 (or_14_out, and_21_out, and_22_out, not_36_out);
  not not_36 (not_36_out, or_11_out);
  or or_15 (or_15_out, and_23_out, and_24_out);
  not not_37 (not_37_out, 1'b1);
  or or_16 (or_16_out, and_20_out, and_19_out);
  not not_38 (not_38_out, or_16_out);
  not not_39 (not_39_out, or_14_out);
  _7_Segment_Display u_7_segment_display_1 (
    .g(not_38_out), .f(not_39_out), .a(not_28_out), .b(not_37_out), .e(not_40_out), .d(not_34_out),
    .c(not_35_out));  // open: dp
  not not_40 (not_40_out, or_15_out);

  // Notes on the sheet:
  //   CRITICO
  //   BAIXO
  //   MEDIO
  //   ALTO
  //   V. ENTRADA
  //   ALARME
  //   ERRO
  //   Gotejamento
  //   Bomba
  //   Bomba
  //   Gotejamento
  //   A0
  //   A1
  //   A2
  //   R
  //   G
  //   B
  //   A
  //   D
  //   C
  //   B
  //   G
  //   F
  //   E
endmodule
